# Fritzing sketch Hook-up (saved by Fritzing 0.9.2b)

parts:
  U1 = ESP8266 WiFi Module [part_number=ESP8266]
  Parte1 = FTDI Basic Programmer
  U2 = V_REG_LD1117VXX [package=78xxl]
  RGB_SMD_LED1 = SMD RGB LED (WS2812) [package=5050]

nets:
  N1: U1.RXD, Parte1.TXO
  N2: U1.VCC, U1.CH_PD, U2.OUT
  N3: U1.GPIO_2, RGB_SMD_LED1.DIn
  GND: U1.GND, Parte1.GND, U2.GND, RGB_SMD_LED1.VSS
  N4: U1.TXD, Parte1.RXI
  VCC: U2.IN, RGB_SMD_LED1.VCC, RGB_SMD_LED1.VDD

notes:
  Fuente externa:5V@4A
  Opcional para monitorear estado
  A siguiente eslabón de la tira.

custom parts:
  ESP8266 WiFi Module: Generic WiFi Module based on the ESP8266 with onboard PCB antenna and UART communications
